# Fritzing sketch Robot Diagram (saved by Fritzing 0.9.3b)
breadboards: 1

parts:
  Raspberry_Pi_1 = Raspberry Pi 3 [part_number=RPI-3-V1.2]  # not connected
  M1 = DC Motor  # not connected
  M2 = DC Motor
  U1 = L298_BRIDGE_DRIVER [package=powerso20]
  VCC1 = 4 x AAA Battery Mount
  Componente1 = Arduino Uno (Rev3) - ICSP

nets:
  N1: M2.pin_1, U1.OUT4
  N2: M2.pin_2, U1.OUT3
  N3: U1.GND, VCC1.-
  N4: U1.IN1, Componente1.D5_PWM
  N5: U1.ENA, Componente1.D4
  N6: U1.IN2, Componente1.D3_PWM
  N7: U1.VSS, VCC1.+
  N8: U1.IN3, Componente1.D9_PWM
  N9: U1.ENB, Componente1.D8
  N10: U1.IN4, Componente1.D7
